# Fritzing sketch all (saved by Fritzing 0.9.3b)
circuit board: 8.46667cm x 5.64444cm
breadboards: 1

parts:
  元件1 = Arduino Nano (Rev3.0)
  元件2 = SHT1x-Breakout
  元件3 = BH1750 digital light sensor
  Squix1 = OLED 0.96" 128x64 I2C SSD1306
  VCC1 = Battery
  Part1 = ML8511 Breakout Board  # not connected

nets (from the breadboard view):
  GND: 元件1.GND, 元件2.GND, 元件3.GND, Squix1.GND, VCC1.+
  VCC: 元件1.VIN, 元件2.VCC, 元件3.VCC, Squix1.VCC, VCC1.-
  N1: 元件1.A5, 元件2.SCK, 元件3.SCL, Squix1.SCL
  N2: 元件1.A4, 元件2.DATA, 元件3.SDA, Squix1.SCA
  N3: 元件1.A1, 元件1.3V3

custom parts:
  BH1750 digital light sensor: BH1750 digital light sensor SKU: 101222
  ML8511 Breakout Board: This breakout board uses the ML8511 UV (ultraviolet) light sensor. The ML8511 works best with light in the 280-390nm wavelengths. The board operates at 2.7 to 3.6V.
