# Fritzing sketch Untitled Sketch 4 (saved by Fritzing 0.9.3b)
circuit board: 8.46667cm x 5.64444cm
breadboards: 1

parts:
  元件1 = Arduino Nano (Rev3.0)
  元件2 = Adafruit SHT31-D Sensirion Temperature/Humidity Sensor [part_number="Adafruit #2857"]
  Squix1 = OLED 0.96" 128x64 I2C SSD1306
  元件3 = BH1750 digital light sensor
  Part1 = ML8511 Breakout Board
  元件4 = Arduino Nano (Rev3.0)
  IC2 = ULN2003A [package="DIP16 [THT]"]
  MOTOR1 = 28BYJ-48 Stepper Motor
  VCC1 = Battery
  VCC2 = Battery

nets:
  3V3: 元件1.D1/TX, 元件1.3V3, Part1.3V3, Part1.EN
  N1: 元件1.D0/RX, Part1.OUT
  GND: 元件1.GND, 元件2.GND, Squix1.GND, 元件3.GND, Part1.GND, VCC1.-
  N2: 元件1.D4, 元件2.SDA, Squix1.SCA, 元件3.SCL, 元件4.D4
  N3: 元件1.D5, 元件2.SCL, Squix1.SCL, 元件3.SDA, 元件4.D5
  VIN: 元件1.VIN, 元件2.VIN, Squix1.VCC, 元件3.VCC, Part1.VIN, VCC1.+
  N4: 元件4.D8, IC2.In_1
  N5: 元件4.D9, IC2.In_2
  N6: 元件4.D10, IC2.In_3
  N7: 元件4.D11/MOSI, IC2.In_4
  N8: 元件4.VIN, IC2.COM_-_Common, MOTOR1.RED, VCC2.+
  N9: 元件4.GND, IC2.0V, VCC2.-
  N10: IC2.Out_4, MOTOR1.BLUE
  N11: IC2.Out_3, MOTOR1.PINK
  N12: IC2.Out_2, MOTOR1.YELLOW
  N13: IC2.Out_1, MOTOR1.ORANGE

custom parts:
  Adafruit SHT31-D Sensirion Temperature/Humidity Sensor: Sensirion Temperature/Humidity sensors are some of the finest & highest-accuracy devices you can get. And, finally we have some that have a true I2C interface for easy reading. The SHT31-D sensor has an excellent ±2% relative humidity and ±0.3°C accuracy for most uses. Unlike earlier SHT sensors, this sensor has a true I2C interface, and (bonus!) even with two address options. It also is 3V or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
  BH1750 digital light sensor: BH1750 digital light sensor SKU: 101222
  ML8511 Breakout Board: This breakout board uses the ML8511 UV (ultraviolet) light sensor. The ML8511 works best with light in the 280-390nm wavelengths. The board operates at 2.7 to 3.6V.
